// Logisim project ALU.circ as structural Verilog: 1 circuit, main circuit main
module main (
  input  A,
  input  B,
  input  AA,
  input  BB,
  input  Cin,
  input  in_6,
  input  in_7,
  input  in_8,
  input  in_9,
  input  AddSub,
  input  in_11,
  input  in_12,
  input  in_13,
  input  in_14,
  output C,
  output out_16,
  output R,
  output out_18,
  output out_19,
  output out_20,
  output out_21,
  output out_22,
  output out_23,
  output out_24,
  output out_25,
  output out_26
);

  wire and_2_out, and_3_out, and_4_out, and_5_out, and_6_out, and_7_out, and_8_out, and_9_out, and_10_out,
       and_11_out, xor_2_out, xor_3_out, xor_5_out, xor_7_out, xor_8_out, xor_10_out, xor_11_out, xor_13_out,
       xor_14_out;

  or or_1 (out_22, and_2_out, and_3_out);
  and and_1 (C, A, B);
  xor xor_1 (R, A, B);
  and and_2 (and_2_out, xor_2_out, in_14);
  and and_3 (and_3_out, xor_3_out, out_21);
  xor xor_2 (xor_2_out, in_8, AddSub);
  xor xor_3 (xor_3_out, xor_2_out, in_14);
  xor xor_4 (out_26, xor_3_out, out_21);
  or or_2 (out_16, and_4_out, and_5_out);
  or or_3 (out_21, and_6_out, and_7_out);
  and and_4 (and_4_out, AA, BB);
  and and_5 (and_5_out, xor_5_out, Cin);
  and and_6 (and_6_out, xor_7_out, in_13);
  and and_7 (and_7_out, xor_8_out, out_20);
  xor xor_5 (xor_5_out, AA, BB);
  xor xor_6 (out_18, xor_5_out, Cin);
  xor xor_7 (xor_7_out, in_9, AddSub);
  xor xor_8 (xor_8_out, xor_7_out, in_13);
  xor xor_9 (out_25, xor_8_out, out_20);
  or or_4 (out_20, and_8_out, and_9_out);
  and and_8 (and_8_out, xor_10_out, in_12);
  and and_9 (and_9_out, xor_11_out, out_19);
  xor xor_10 (xor_10_out, in_7, AddSub);
  xor xor_11 (xor_11_out, xor_10_out, in_12);
  xor xor_12 (out_24, xor_11_out, out_19);
  or or_5 (out_19, and_10_out, and_11_out);
  and and_10 (and_10_out, xor_13_out, in_11);
  and and_11 (and_11_out, xor_14_out, AddSub);
  xor xor_13 (xor_13_out, in_6, AddSub);
  xor xor_14 (xor_14_out, xor_13_out, in_11);
  xor xor_15 (out_23, xor_14_out, AddSub);

  // Notes on the sheet:
  //   Half Adder
  //   Full adder
  //   Giant mess of gates which is apparently an ALU
endmodule
